# Fritzing sketch GatewayElectronicStepV3-1 (saved by Fritzing 0.9.3b)
circuit board: 8.46667cm x 5.64444cm
breadboards: 2

parts:
  U1 = Voltage Regulator - 3.3V [package="TO220 [THT]"]
  C3 = Electrolytic Capacitor [capacitance=100μF package="0807 [SMD, electrolytic]"]
  MOD-WIFI-ESP8266-DEV1 = Olimex ESP8266 DEV
  ULN1 = Darlington Driver [package=dil18]
  LED2 = smd LED [color="Red (633nm)" package="0603 [SMD]"]
  LED3 = smd LED [color="Blue (525nm)" package="1206 [SMD]"]
  LED4 = smd LED [color="Green (570nm)" package="0805 [SMD]"]
  R2 = Resistor [tolerance=±5% resistance=1k package=THT]
  R8 = Resistor [tolerance=±5% resistance=3.3k package=THT]
  R9 = Resistor [tolerance=±5% resistance=1k package=THT]
  R13 = Resistor [tolerance=±5% resistance=33k package="2512 [SMD]"]
  R14 = 2.7k Ω Resistor [package=THT]
  R16 = 2k Ω Resistor [package=THT]
  U2 = Hirose DF13 Series Header [part_number=DF13#-2P-1.25V package=DF13C-2P-1.25V]
  U4 = Hirose DF13 Series Header [part_number=DF13#-3P-1.25V package=DF13C-3P-1.25V]
  U5 = Hirose DF13 Series Header [part_number=DF13#-2P-1.25V package=DF13C-2P-1.25V]
  R18 = Resistor [tolerance=±5% resistance=220 package=THT]
  U6 = Hirose DF13 Series Header [part_number=DF13#-3P-1.25V package=DF13C-3P-1.25V]
  U7 = Hirose DF13 Series Header [part_number=DF13#-3P-1.25V package=DF13C-3P-1.25V]
  R19 = Resistor [tolerance=±5% resistance=1k package=THT]
  Q2 = TRANSISTOR_NPN [package=to-92]
  Q3 = TRANSISTOR_NPN [package=to-92]
  R20 = Resistor [tolerance=±5% resistance=1k package=THT]
  R21 = Resistor [tolerance=±5% resistance=1k package=THT]
  R22 = Resistor [tolerance=±5% resistance=1k package=THT]
  R23 = Resistor [tolerance=±5% resistance=1k package=THT]
  U3 = Hirose DF13 Series Header [part_number=DF13#-5P-1.25V package=DF13C-5P-1.25V]
  U9 = Hirose DF13 Series Header [part_number=DF13#-4P-1.25V package=DF13C-4P-1.25V]
  U10 = Hirose DF13 Series Header [part_number=DF13#-3P-1.25V package=DF13C-3P-1.25V]

nets:
  GND: U1.GND, C3.-, C3.+, MOD-WIFI-ESP8266-DEV1.GND, MOD-WIFI-ESP8266-DEV1.GPIO16, MOD-WIFI-ESP8266-DEV1.GPIO15, MOD-WIFI-ESP8266-DEV1.GPIO2, ULN1.9, R16.Pin_0, R16.Pin_1, U2.1, U4.1, R18.Pin_1, U6.3, Q2.C, Q3.C, R23.Pin_0, U3.4, U9.4
  N1: U1.Output, MOD-WIFI-ESP8266-DEV1.3.3V, R13.Pin_0
  N2: U1.Input_voltage, R2.Pin_1, R8.Pin_1, R14.Pin_1, U2.2
  N3: MOD-WIFI-ESP8266-DEV1.GPIO1, U7.2
  N4: MOD-WIFI-ESP8266-DEV1.GPIO3, U6.2
  N5: MOD-WIFI-ESP8266-DEV1.GPIO5, R9.Pin_0
  N6: MOD-WIFI-ESP8266-DEV1.RSTB, ULN1.11, LED2.cathode
  N7: MOD-WIFI-ESP8266-DEV1.GPIO12, ULN1.6
  N8: MOD-WIFI-ESP8266-DEV1.GPIO14, ULN1.2
  N9: MOD-WIFI-ESP8266-DEV1.GPIO13, ULN1.8
  N10: MOD-WIFI-ESP8266-DEV1.GPIO0, U5.1
  N11: MOD-WIFI-ESP8266-DEV1.GPIO4, U4.2
  N12: ULN1.13, LED4.cathode
  N13: ULN1.17, LED3.cathode
  N14: LED2.anode, R8.Pin_0
  N15: LED3.anode, R14.Pin_0
  N16: LED4.anode, R2.Pin_0
  N17: R9.Pin_1, U10.2
  N18: R13.Pin_1, U4.3
  N19: U5.2, R18.Pin_0
  N20: U6.1, U9.3
  N21: U7.1, U9.2
  N22: U7.3, R19.Pin_0
  N23: R19.Pin_1, Q2.B
  N24: Q2.E, R20.Pin_0
  N25: Q3.E, R21.Pin_0
  N26: Q3.B, R22.Pin_0
  N27: R20.Pin_1, R21.Pin_1, R22.Pin_1, U3.2, U3.5
  N28: R23.Pin_1, U3.3
  N29: U3.1, U10.3
  N30: U9.1, U10.1

notes:
  +5V Power source
  +3.3V
  3.3v Rx Tx
  5v Tx RX
  readyPin
  C1
  1 pin connector
  C2
  3 pins connector
  3.3v serial
  ground
  GPIO 2
  GPIO 4
  +3.3v
  5v Serial + ready pin
  + 5v reference from arduino

custom parts:
  Voltage Regulator - 3.3V: 3.3V DC Voltage Regulator
  Olimex ESP8266 DEV: MOD-WIFI-ESP8266-DEV is the ultimate development board for ESP8266 with all GPIOs and resources exposed, can be soldered to PCB or used with breadboard and UEXT. Small U.FL connector is provided for external antenna connection. ESP8266 is very highly integrated SOC which includes Xtensa LX106 core processor, RAM, RF front end and allow WIFI TCP-IP stack to be implemented on board with just few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
  2.7k Ω Resistor: A generic resistor (0.25W)
  2k Ω Resistor: A generic 5-band resistor (0.25W)
