# Fritzing sketch serial33to5v (saved by Fritzing 0.9.3b)
circuit board: 8.46667cm x 5.64444cm
breadboards: 1

parts:
  R1 = 2k Ω Resistor [package=THT]
  R7 = Resistor [tolerance=±5% resistance=1k package="2010 [SMD]"]
  R8 = Resistor [tolerance=±5% resistance=1k package="2010 [SMD]"]  # not connected
  R10 = Resistor [tolerance=±5% resistance=1k package="2010 [SMD]"]
  Q7 = NPN-Transistor [package="TO92 [THT]"]
  Q8 = NPN-Transistor [package="TO92 [THT]"]
  R11 = Resistor [tolerance=±5% resistance=1k package="2010 [SMD]"]
  R12 = Resistor [tolerance=±5% resistance=1k package="2010 [SMD]"]
  JP8 = Header 4 [package=molex-1x4_lock]
  JP9 = Header 4 [package=molex-1x4_lock]

nets (from the pcb view):
  N1: R1.Pin_0, R12.Pin_0, JP8.RX_3.3v
  N2: R1.Pin_1, JP9.RX_3.3v
  N3: R7.Pin_0, Q8.C, R11.Pin_1
  N4: R7.Pin_1, Q7.B
  N5: R10.Pin_0, JP9.TX_3.3v
  N6: R10.Pin_1, Q8.B
  N7: Q7.E, Q8.E, R12.Pin_1, JP8.Ground, JP9.Ground
  N8: Q7.C, JP8.TX_3.3v

custom parts:
  2k Ω Resistor: A generic 5-band resistor (0.25W)
  Header 4: Header 4 Standard 4-pin 0.1 header. Use with straight break away headers (SKU : PRT-00116), right angle break away headers (PRT-00553), swiss pins (PRT-00743), machine pins (PRT-00117), and female headers (PRT-00115). Molex polarized connector foot print use with SKU : PRT-08231 with associated crimp pins and housings. 1MM SMD Version SKU: PRT-10208
